# Fritzing sketch envNodePCB (saved by Fritzing 0.9.3b)
circuit board: 6.5cm x 5.5cm
breadboards: 1

parts:
  SPARKFUN_THING_DEV = SparkFun ESP8266 Thing
  DHT22 = Humidity and Temperature Sensor RHT03 [part_number=DHT22]
  LDR = Photocell (LDR) [package=THT]
  7_5kΩ = Resistor [tolerance=±5% resistance=7.5k package=THT]
  3kΩ = Resistor [tolerance=±5% resistance=3k package=THT]

nets:
  N1: SPARKFUN_THING_DEV.GND, DHT22.GND_2, 3kΩ.Pin_1
  VCC: SPARKFUN_THING_DEV.VCC, DHT22.Vcc, 7_5kΩ.Pin_1
  N2: SPARKFUN_THING_DEV.GPIO16, DHT22.Data-signal
  N3: SPARKFUN_THING_DEV.ADC, LDR.pin_1, 3kΩ.Pin_0
  N4: LDR.pin_0, 7_5kΩ.Pin_0

notes:
  homeBakedPi EnvNode
